// Logisim project Nono.circ as structural Verilog
module decodeur (
  input  [3:0] op,
  output isLoad,
  output regWrite,
  output isJMP,
  output [2:0] ctrlUAL
);

  wire and_2_out, not_1_out, not_2_out;

  and and_1 (isLoad, op[3], ~op[2], op[1], op[0]);  // AND_Gate
  and and_2 (and_2_out, ~op[3], op[2], ~op[1], ~op[0]);  // AND_Gate
  not not_1 (not_1_out, and_2_out);
  and and_3 (isJMP, op[2], not_1_out);
  and and_4 (regWrite, ~isLoad, ~isJMP);  // AND_Gate
  Multiplexer #(.width(3)) multiplexer_1 (
    .in0({2'b00, isJMP}), .in1(op[2:0]), .out(ctrlUAL), .sel(not_2_out));  // open: en
  not not_2 (not_2_out, isJMP);
endmodule

module UAL (
  input  [7:0] A,
  input  [7:0] B,
  input  [2:0] ctrlUAL,
  output [7:0] S,
  output [3:0] flags
);

  wire adder_1_cout, subtractor_1_bout;
  wire [7:0] adder_1_out, AND_out, NOT_out, OR_out, shifter_1_out, shifter_2_out, subtractor_1_out;

  Adder adder_1 (.a(A), .b(B), .out(adder_1_out), .cout(adder_1_cout));  // open: cin
  or CF (flags[3], subtractor_1_bout, adder_1_cout);
  Subtractor subtractor_1 (.a(A), .b(B), .out(subtractor_1_out), .bout(subtractor_1_bout));  // open: bin
  Multiplexer #(.select(3), .width(8)) multiplexer_1 (
    .in0(adder_1_out), .in1(subtractor_1_out), .in2(OR_out), .in3(AND_out), .in4(NOT_out),
    .in5(shifter_1_out), .in6(shifter_2_out), .out({flags[1], S[6:0]}), .sel(ctrlUAL));  // open: in7, en
  assign OR_out = B | A;  // OR_Gate OR, 8 bits wide
  and ZF (flags[2], ~S[0], ~S[1], ~S[2], ~S[3], ~S[4], ~S[5], ~S[6], ~flags[1]);  // AND_Gate
  assign AND_out = B & A;  // AND_Gate AND, 8 bits wide
  assign NOT_out = ~A;  // NOT_Gate NOT, 8 bits wide
  Shifter shifter_1 (.in(A), .\dist (3'b001), .out(shifter_1_out));
  Shifter #(.shift("lr")) shifter_2 (.in(A), .\dist (3'b001), .out(shifter_2_out));
  and OF (flags[0], B[7], A[7]);

  assign S[7] = flags[1];

  // Notes on the sheet:
  //   add
  //   sub
  //   S
  //   SF
  //   <<
  //   >>
endmodule

module Controle_de_saut (
  input  [3:0] op,
  input  [3:0] flags,
  output [1:0] PC
);

  wire and_1_out, and_2_out, and_3_out, and_4_out, and_5_out, and_6_out, and_7_out, and_8_out, and_9_out,
       and_10_out, and_11_out, e1_out, not_1_out;

  and and_1 (and_1_out, ~op[3], ~op[1], op[0]);  // AND_Gate
  and and_2 (and_2_out, ~op[3], flags[2]);  // AND_Gate
  and and_3 (and_3_out, ~flags[2], flags[1], op[0]);  // AND_Gate
  and and_4 (and_4_out, ~op[3], op[1], op[0], ~flags[2]);  // AND_Gate
  and and_5 (and_5_out, ~op[3], op[1], op[0], ~flags[2], ~flags[1]);  // AND_Gate
  and and_6 (and_6_out, op[3], flags[2]);
  and and_7 (and_7_out, op[3], ~op[1], op[0], ~flags[2], flags[1]);  // AND_Gate
  and and_8 (and_8_out, op[3], op[1], ~op[0], ~flags[2], flags[1]);  // AND_Gate
  and and_9 (and_9_out, op[3], ~op[1], ~op[0], ~flags[2], ~flags[1]);  // AND_Gate
  or e1 (e1_out, and_1_out, and_2_out, and_3_out, and_4_out, and_5_out, and_6_out, and_7_out, and_8_out, and_9_out);
  and and_10 (and_10_out, op[2], e1_out);
  and and_11 (and_11_out, ~op[0], ~op[1], op[2], ~op[3]);  // AND_Gate
  not not_1 (not_1_out, and_11_out);
  and and_12 (PC[1], and_10_out, not_1_out);

  assign PC[0] = op[2];

  // Notes on the sheet:
  //   refaire les portes voir nos tableau de verité
  //   Halt
  //   e0
endmodule
