// Logisim project UAL.circ as structural Verilog: 1 circuit, main circuit main
module main (
  input  [7:0] A,
  input  [7:0] B,
  input  [2:0] ctrlUAL,
  output [7:0] S,
  output [3:0] flags
);

  wire adder_1_cout, CF_out, subtractor_1_bout;
  wire [7:0] adder_1_out, and_1_out, not_1_out, not_2_out, or_1_out, shifter_1_out, shifter_2_out,
       subtractor_1_out, ZF_out;

  Adder adder_1 (.a(A), .b(B), .out(adder_1_out), .cout(adder_1_cout));  // open: cin
  or CF (CF_out, subtractor_1_bout, adder_1_cout);
  Subtractor subtractor_1 (.a(A), .b(B), .out(subtractor_1_out), .bout(subtractor_1_bout));  // open: bin
  Multiplexer #(.select(3), .width(8)) multiplexer_1 (
    .in0(adder_1_out), .in1(subtractor_1_out), .in2(or_1_out), .in3(and_1_out), .in4(not_2_out),
    .in5(shifter_1_out), .in6(shifter_2_out), .out(S), .sel(ctrlUAL));  // open: in7, en
  assign ZF_out = S | {8{1'b0}};  // OR_Gate ZF, 8 bits wide
  assign not_1_out = ~ZF_out;  // NOT_Gate not_1, 8 bits wide
  assign or_1_out = B | A;  // OR_Gate or_1, 8 bits wide
  assign and_1_out = B & A;  // AND_Gate and_1, 8 bits wide
  assign not_2_out = ~A;  // NOT_Gate not_2, 8 bits wide
  Shifter shifter_1 (.in(A), .\dist (3'b001), .out(shifter_1_out));
  Shifter #(.shift("lr")) shifter_2 (.in(A), .\dist (3'b001), .out(shifter_2_out));
endmodule
